// Logisim project Serie_9.circ as structural Verilog: 5 circuits, main circuit main
module main (
  input  x,
  input  y,
  input  c,
  input  in_4,
  input  in_5,
  input  in_6,
  input  in_7,
  input  in_8,
  input  in_9,
  input  in_10,
  input  in_11,
  input  in_12,
  input  in_13,
  input  in_14,
  input  in_15,
  input  in_16,
  input  in_17,
  input  in_18,
  input  in_19,
  input  in_20,
  input  in_21,
  output s_Ha,
  output c_HA,
  output Cout_FA,
  output s_FA,
  output out_26,
  output out_27,
  output out_28,
  output out_29,
  output out_30,
  output out_31,
  output out_32,
  output out_33,
  output out_34,
  output out_35
);

  FA fa_1 (.Cin(c), .x(x), .y(y), .s(s_FA), .Cout(Cout_FA));
  HA ha_1 (.x(x), .y(y), .s(s_Ha), .Cout(c_HA));
  Ripple_Carry_Adder_4_bit ripple_carry_adder_4_bit_1 (
    .x3(in_4), .y3(in_5), .x2(in_6), .y2(in_7), .x1(in_8), .y1(in_9), .x0(in_10), .y0(in_11), .Cin(in_12),
    .Cout(out_26), .s3(out_27), .s2(out_28), .s1(out_29), .s0(out_30));
  ADDSUB_4_bit addsub_4_bit_1 (
    .x3(in_13), .y3(in_14), .x2(in_15), .y2(in_16), .x1(in_17), .y1(in_18), .x0(in_19), .y0(in_20),
    .op(in_21), .Cout(out_31), .s3(out_32), .s2(out_33), .s1(out_34), .s0(out_35));

  // Notes on the sheet:
  //   1-bit Addition
endmodule

module HA (
  input  x,
  input  y,
  output s,
  output Cout
);

  xor xor_1 (s, x, y);
  and and_1 (Cout, x, y);
endmodule

module FA (
  input  Cin,
  input  x,
  input  y,
  output s,
  output Cout
);

  wire ha_1_cout, ha_1_s, ha_2_cout;

  HA ha_1 (.x(x), .y(y), .s(ha_1_s), .Cout(ha_1_cout));
  HA ha_2 (.x(Cin), .y(ha_1_s), .s(s), .Cout(ha_2_cout));
  or or_1 (Cout, ha_2_cout, ha_1_cout);
endmodule

module Ripple_Carry_Adder_4_bit (
  input  x3,
  input  y3,
  input  x2,
  input  y2,
  input  x1,
  input  y1,
  input  x0,
  input  y0,
  input  Cin,
  output Cout,
  output s3,
  output s2,
  output s1,
  output s0
);

  wire fa_2_cout, fa_3_cout, fa_4_cout;

  FA fa_1 (.Cin(fa_2_cout), .x(x3), .y(y3), .s(s3), .Cout(Cout));
  FA fa_2 (.Cin(fa_3_cout), .x(x2), .y(y2), .s(s2), .Cout(fa_2_cout));
  FA fa_3 (.Cin(fa_4_cout), .x(x1), .y(y1), .s(s1), .Cout(fa_3_cout));
  FA fa_4 (.Cin(Cin), .x(x0), .y(y0), .s(s0), .Cout(fa_4_cout));
endmodule

module ADDSUB_4_bit (
  input  x3,
  input  y3,
  input  x2,
  input  y2,
  input  x1,
  input  y1,
  input  x0,
  input  y0,
  input  op,
  output Cout,
  output s3,
  output s2,
  output s1,
  output s0
);

  wire fa_2_cout, fa_3_cout, fa_4_cout, xor_1_out, xor_2_out, xor_3_out, xor_4_out;

  xor xor_1 (xor_1_out, y3, op);
  FA fa_1 (.Cin(fa_2_cout), .x(x3), .y(xor_1_out), .s(s3), .Cout(Cout));
  xor xor_2 (xor_2_out, y2, op);
  FA fa_2 (.Cin(fa_3_cout), .x(x2), .y(xor_2_out), .s(s2), .Cout(fa_2_cout));
  FA fa_3 (.Cin(fa_4_cout), .x(x1), .y(xor_3_out), .s(s1), .Cout(fa_3_cout));
  xor xor_3 (xor_3_out, y1, op);
  FA fa_4 (.Cin(op), .x(x0), .y(xor_4_out), .s(s0), .Cout(fa_4_cout));
  xor xor_4 (xor_4_out, y0, op);
endmodule
